// Logisim project Mycelium_01.circ as structural Verilog
module main (
  input  [44:0] ramcode_in,
  input  [15:0] data_in,
  input  CLK,
  input  [15:0] in_4,
  input  [15:0] in_5,
  input  [15:0] in_6,
  input  [15:0] in_7,
  input  [15:0] in_8,
  input  [15:0] in_9,
  input  [15:0] in_10,
  input  [15:0] in_11,
  input  [15:0] in_12,
  input  [15:0] in_13,
  input  [15:0] in_14,
  input  [15:0] in_15,
  input  [15:0] in_16,
  input  [15:0] in_17,
  input  [15:0] in_18,
  input  [15:0] in_19,
  input  [15:0] in_20,
  input  [15:0] in_21,
  input  [15:0] in_22,
  input  [15:0] in_23,
  input  [15:0] in_24,
  input  [15:0] in_25,
  input  [15:0] in_26,
  input  [15:0] in_27,
  input  [15:0] in_28,
  input  [15:0] in_29,
  input  [15:0] in_30,
  input  [15:0] in_31,
  input  [15:0] in_32,
  input  [15:0] in_33,
  input  [15:0] in_34,
  input  [15:0] in_35,
  output [15:0] data_addrbus,
  output [15:0] data_bus,
  output [15:0] adrbus,
  output ram_enable,
  output [15:0] out_40,
  output [15:0] out_41,
  output [15:0] out_42,
  output [15:0] out_43,
  output [15:0] out_44,
  output [15:0] out_45,
  output [15:0] out_46,
  output [15:0] out_47,
  output [15:0] out_48,
  output [15:0] out_49,
  output [15:0] out_50,
  output [15:0] out_51,
  output [15:0] out_52,
  output [15:0] out_53,
  output [15:0] out_54,
  output [15:0] out_55,
  output [15:0] out_56,
  output [15:0] out_57,
  output [15:0] out_58,
  output [15:0] out_59,
  output [15:0] out_60,
  output [15:0] out_61,
  output [15:0] out_62,
  output [15:0] out_63,
  output [15:0] out_64,
  output [15:0] out_65,
  output [15:0] out_66,
  output [15:0] out_67,
  output [15:0] out_68,
  output [15:0] out_69,
  output [15:0] out_70,
  output [15:0] out_71
);

  wire and_1_out, bit_extender_4_out, buffer_3_out, comparator_1_eq, comparator_2_eq, comparator_4_gt,
       comparator_4_lt, controlled_buffer_2_out, conv_1_o, conv_1_o_2, conv_2_o, conv_2_o_2, conv_3_o,
       conv_3_o_2, conv_4_o, conv_5_o, conv_6_o, conv_7_o, conv_8_o, conv_9_o, conv_10_o, conv_11_o,
       conv_12_o, conv_13_o, conv_14_o, conv_15_o, not_1_out, not_2_out, not_3_out, or_7_out;
  wire [1:0] bit_extender_8_out;
  wire [2:0] bit_extender_2_out, bit_extender_3_out, bit_extender_6_out, bit_extender_7_out,
       bit_extender_9_out, bit_extender_10_out, bit_extender_12_out, bit_extender_13_out,
       bit_extender_14_out, bit_extender_15_out, bit_extender_16_out, multiplexer_3_out, multiplexer_5_out,
       or_3_out, or_4_out;
  wire [4:0] bit_extender_1_out, bit_extender_5_out;
  wire [7:0] demultiplexer_3_out0, demultiplexer_3_out1, demultiplexer_3_out2, demultiplexer_3_out4,
       demultiplexer_3_out6;
  wire [15:0] a, alu_1_output_bus_1, AX_q, bit_extender_11_out, buffer_2_out, bx_q, controlled_buffer_1_out,
       controlled_buffer_5_out, controlled_buffer_9_out, CS_q, cx_q, demultiplexer_1_out0,
       demultiplexer_1_out1, demultiplexer_1_out2, demultiplexer_1_out3, demultiplexer_1_out6,
       demultiplexer_1_out7, demultiplexer_1_out8, demultiplexer_1_out9, demultiplexer_2_out0,
       demultiplexer_2_out1, demultiplexer_2_out2, demultiplexer_2_out3, demultiplexer_2_out5,
       demultiplexer_2_out6, demultiplexer_2_out7, demultiplexer_2_out8, demultiplexer_2_out9,
       demultiplexer_5_out0, demultiplexer_5_out1, demultiplexer_6_out0, demultiplexer_6_out1,
       demultiplexer_7_out0, demultiplexer_7_out1, demultiplexer_8_out0, demultiplexer_8_out1,
       demultiplexer_8_out2, demultiplexer_8_out3, demultiplexer_8_out4, demultiplexer_8_out5,
       demultiplexer_9_out0, demultiplexer_9_out1, DS_q, dx_q, IP_q, lu_1_output_bus_1, multiplexer_1_out,
       multiplexer_2_out, multiplexer_4_out, multiplexer_6_out, multiplexer_7_out, or_1_out, or_2_out,
       or_5_out, or_6_out, SC_q, sflags_q, stack_dout;
  wire [44:0] debug_panel2_sw13;

  DipSwitch #(.number(32)) debug_panel (
    .sw1(debug_panel2_sw13[44]), .sw2(debug_panel2_sw13[43]), .sw3(debug_panel2_sw13[42]),
    .sw4(debug_panel2_sw13[41]), .sw5(debug_panel2_sw13[40]), .sw6(debug_panel2_sw13[39]),
    .sw7(debug_panel2_sw13[38]), .sw8(debug_panel2_sw13[37]), .sw9(debug_panel2_sw13[36]),
    .sw10(debug_panel2_sw13[35]), .sw11(debug_panel2_sw13[34]), .sw12(debug_panel2_sw13[33]),
    .sw13(debug_panel2_sw13[32]), .sw14(debug_panel2_sw13[31]), .sw15(debug_panel2_sw13[30]),
    .sw16(debug_panel2_sw13[29]), .sw17(debug_panel2_sw13[28]), .sw18(debug_panel2_sw13[27]),
    .sw19(debug_panel2_sw13[26]), .sw20(debug_panel2_sw13[25]), .sw21(debug_panel2_sw13[24]),
    .sw22(debug_panel2_sw13[23]), .sw23(debug_panel2_sw13[22]), .sw24(debug_panel2_sw13[21]),
    .sw25(debug_panel2_sw13[20]), .sw26(debug_panel2_sw13[19]), .sw27(debug_panel2_sw13[18]),
    .sw28(debug_panel2_sw13[17]), .sw29(debug_panel2_sw13[16]), .sw30(debug_panel2_sw13[15]),
    .sw31(debug_panel2_sw13[14]), .sw32(debug_panel2_sw13[13]));
  DipSwitch #(.number(13)) debug_panel2 (
    .sw1(debug_panel2_sw13[12]), .sw2(debug_panel2_sw13[11]), .sw3(debug_panel2_sw13[10]),
    .sw4(debug_panel2_sw13[9]), .sw5(debug_panel2_sw13[8]), .sw6(debug_panel2_sw13[7]),
    .sw7(debug_panel2_sw13[6]), .sw8(debug_panel2_sw13[5]), .sw9(debug_panel2_sw13[4]),
    .sw10(debug_panel2_sw13[3]), .sw11(debug_panel2_sw13[2]), .sw12(debug_panel2_sw13[1]),
    .sw13(debug_panel2_sw13[0]));
  Bit_Extender #(.in_width(16), .out_width(5)) bit_extender_1 (.in(demultiplexer_2_out9), .out(bit_extender_1_out));
  Comparator #(.width(5)) comparator_1 (.a(ramcode_in[44:40]), .b(5'b01001), .eq(comparator_1_eq));  // open: gt, lt
  Demultiplexer #(.enable("false"), .select(5), .width(16)) demultiplexer_1 (
    .out0(demultiplexer_1_out0), .out1(demultiplexer_1_out1), .out2(demultiplexer_1_out2),
    .out3(demultiplexer_1_out3), .out6(demultiplexer_1_out6), .out7(demultiplexer_1_out7),
    .out8(demultiplexer_1_out8), .out9(demultiplexer_1_out9), .in(ramcode_in[39:24]), .sel(ramcode_in[44:40]));  // open: out4, out5, out10, out11, out12, out13, out14, out15, out16, out17, out18, out19, out20, out21, out22, out23, out24, out25, out26, out27, out28, out29, out30, out31
  Demultiplexer #(.enable("false"), .select(5), .width(16)) demultiplexer_2 (
    .out0(demultiplexer_2_out0), .out1(demultiplexer_2_out1), .out2(demultiplexer_2_out2),
    .out3(demultiplexer_2_out3), .out4(a), .out5(demultiplexer_2_out5), .out6(demultiplexer_2_out6),
    .out7(demultiplexer_2_out7), .out8(demultiplexer_2_out8), .out9(demultiplexer_2_out9),
    .in(ramcode_in[23:8]), .sel(ramcode_in[44:40]));  // open: out10, out11, out12, out13, out14, out15, out16, out17, out18, out19, out20, out21, out22, out23, out24, out25, out26, out27, out28, out29, out30, out31
  Demultiplexer #(.enable("false"), .select(5), .width(8)) demultiplexer_3 (
    .out0(demultiplexer_3_out0), .out1(demultiplexer_3_out1), .out2(demultiplexer_3_out2),
    .out4(demultiplexer_3_out4), .out6(demultiplexer_3_out6), .in(ramcode_in[7:0]), .sel(ramcode_in[44:40]));  // open: out3, out5, out7, out8, out9, out10, out11, out12, out13, out14, out15, out16, out17, out18, out19, out20, out21, out22, out23, out24, out25, out26, out27, out28, out29, out30, out31
  assign controlled_buffer_1_out = comparator_1_eq ? multiplexer_6_out : 16'bz;  // Controlled_Buffer controlled_buffer_1
  Demultiplexer #(.enable("false"), .select(5), .width(16)) demultiplexer_4 (
    .out0(out_40), .out1(out_41), .out2(out_42), .out3(out_43), .out4(out_44), .out5(out_45), .out6(out_46),
    .out7(out_47), .out8(out_48), .out9(out_49), .out10(out_50), .out11(out_51), .out12(out_52),
    .out13(out_53), .out14(out_54), .out15(out_55), .out16(out_56), .out17(out_57), .out18(out_58),
    .out19(out_59), .out20(out_60), .out21(out_61), .out22(out_62), .out23(out_63), .out24(out_64),
    .out25(out_65), .out26(out_66), .out27(out_67), .out28(out_68), .out29(out_69), .out30(out_70),
    .out31(out_71), .in(controlled_buffer_1_out), .sel(bit_extender_5_out));
  Multiplexer #(.enable("false"), .select(5), .width(16)) multiplexer_1 (
    .in0(in_4), .in1(in_5), .in2(in_6), .in3(in_7), .in4(in_8), .in5(in_9), .in6(in_10), .in7(in_11),
    .in8(in_12), .in9(in_13), .in10(in_14), .in11(in_15), .in12(in_16), .in13(in_17), .in14(in_18),
    .in15(in_19), .in16(in_20), .in17(in_21), .in18(in_22), .in19(in_23), .in20(in_24), .in21(in_25),
    .in22(in_26), .in23(in_27), .in24(in_28), .in25(in_29), .in26(in_30), .in27(in_31), .in28(in_32),
    .in29(in_33), .in30(in_34), .in31(in_35), .out(multiplexer_1_out), .sel(bit_extender_1_out));
  Bit_Extender #(.in_width(16), .out_width(3)) bit_extender_2 (.in(demultiplexer_1_out9), .out(bit_extender_2_out));
  lu lu_1 (
    .Output_bus_1(lu_1_output_bus_1), .f(demultiplexer_3_out6), .in2(multiplexer_6_out),
    .in1(demultiplexer_1_out6));
  Demultiplexer #(.enable("false"), .width(16)) demultiplexer_5 (
    .out0(demultiplexer_5_out0), .out1(demultiplexer_5_out1), .in(demultiplexer_2_out1), .sel(comparator_2_eq));
  Bit_Extender #(.in_width(16), .out_width(3)) bit_extender_3 (.in(demultiplexer_2_out3), .out(bit_extender_3_out));
  Comparator #(.mode("unsigned")) comparator_2 (
    .a(demultiplexer_3_out1), .b(8'h81), .eq(comparator_2_eq));  // open: gt, lt
  Comparator #(.mode("unsigned")) comparator_3 (.a(demultiplexer_3_out2), .b(8'h1), .eq(ram_enable));  // open: gt, lt
  Counter #(.max('hffff), .width(16)) IP (
    .load(controlled_buffer_2_out), .clk(CLK), .D(demultiplexer_5_out0), .Q(IP_q));  // open: clr, up, count, carry
  not not_1 (not_1_out, and_1_out);
  Bit_Extender #(.in_width(16), .out_width(1), .\type ("one")) bit_extender_4 (
    .in(demultiplexer_5_out0), .out(bit_extender_4_out));
  assign controlled_buffer_2_out = not_1_out ? bit_extender_4_out : 1'bz;  // Controlled_Buffer controlled_buffer_2
  Bit_Extender #(.in_width(16), .out_width(5)) bit_extender_5 (.in(demultiplexer_1_out8), .out(bit_extender_5_out));
  Bit_Extender #(.in_width(16), .out_width(3)) bit_extender_6 (.in(demultiplexer_1_out0), .out(bit_extender_6_out));
  Demultiplexer #(.enable("false"), .width(16)) demultiplexer_6 (
    .out0(demultiplexer_6_out0), .out1(demultiplexer_6_out1), .in(demultiplexer_1_out2), .sel(ram_enable));
  Bit_Extender #(.in_width(16), .out_width(3)) bit_extender_7 (.in(demultiplexer_2_out5), .out(bit_extender_7_out));
  Bit_Extender #(.out_width(2)) bit_extender_8 (.in(demultiplexer_3_out0), .out(bit_extender_8_out));
  conv conv_9 (.o(conv_9_o), .Input_bus_1(demultiplexer_1_out1));
  conv conv_1 (.o(conv_1_o), .Input_bus_1(demultiplexer_1_out0));
  conv conv_2 (.o(conv_2_o), .Input_bus_1(alu_1_output_bus_1));
  assign multiplexer_1_out = alu_1_output_bus_1;  // Buffer buffer_1, 16 bits wide
  alu alu_1 (
    .Output_bus_1(alu_1_output_bus_1), .func(bit_extender_8_out), .in1(controlled_buffer_5_out),
    .in2(demultiplexer_2_out0));
  assign multiplexer_1_out = demultiplexer_3_out6[7] ? lu_1_output_bus_1 : 16'bz;  // Controlled_Buffer controlled_buffer_3
  conv conv_7 (.o(conv_7_o), .Input_bus_1(demultiplexer_6_out0));
  Multiplexer #(.enable("false"), .width(16)) multiplexer_2 (
    .in0(demultiplexer_2_out2), .in1(demultiplexer_6_out1), .out(multiplexer_2_out), .sel(ram_enable));
  Demultiplexer #(.enable("false"), .width(16)) demultiplexer_7 (
    .out0(demultiplexer_7_out0), .out1(demultiplexer_7_out1), .in(multiplexer_2_out), .sel(ram_enable));
  Register #(.width(16)) CS (.D(demultiplexer_1_out1), .clk(conv_9_o), .Q(CS_q));  // open: en, clr
  assign or_1_out = multiplexer_7_out | demultiplexer_1_out3;  // OR_Gate or_1, 16 bits wide
  assign multiplexer_1_out = conv_7_o ? controlled_buffer_9_out : 16'bz;  // Controlled_Buffer controlled_buffer_4
  Bit_Extender #(.in_width(16), .out_width(3)) bit_extender_9 (.in(demultiplexer_6_out0), .out(bit_extender_9_out));
  Bit_Extender #(.in_width(16), .out_width(3)) bit_extender_10 (.in(demultiplexer_5_out1), .out(bit_extender_10_out));
  assign bit_extender_11_out = {{8{demultiplexer_3_out4[7]}}, demultiplexer_3_out4};  // Bit_Extender bit_extender_11
  conv conv_13 (.o(conv_13_o), .Input_bus_1(bit_extender_11_out));
  assign controlled_buffer_5_out = conv_1_o ? multiplexer_6_out : 16'bz;  // Controlled_Buffer controlled_buffer_5
  assign or_2_out = or_1_out | multiplexer_1_out;  // OR_Gate or_2, 16 bits wide
  Demultiplexer #(.enable("false"), .select(3), .width(16)) demultiplexer_8 (
    .out0(demultiplexer_8_out0), .out1(demultiplexer_8_out1), .out2(demultiplexer_8_out2),
    .out3(demultiplexer_8_out3), .out4(demultiplexer_8_out4), .out5(demultiplexer_8_out5), .in(or_2_out),
    .sel(multiplexer_3_out));  // open: out6, out7
  conv conv_5 (.o(conv_5_o), .Input_bus_1(demultiplexer_8_out1));
  Multiplexer #(.enable("false"), .width(3)) multiplexer_3 (
    .in0(or_3_out), .in1(3'b000), .out(multiplexer_3_out), .sel(conv_2_o));
  assign or_3_out = bit_extender_6_out | bit_extender_7_out | bit_extender_2_out | bit_extender_3_out | bit_extender_15_out;  // OR_Gate or_3, 3 bits wide
  Adder #(.width(16)) adder_1 (.a(DS_q), .b(demultiplexer_7_out0), .out(data_addrbus));  // open: cin, cout
  Adder #(.width(16)) adder_2 (.a(CS_q), .b(IP_q), .out(adrbus));  // open: cin, cout
  Demultiplexer #(.enable("false"), .width(16)) demultiplexer_9 (
    .out0(demultiplexer_9_out0), .out1(demultiplexer_9_out1), .in(a), .sel(conv_13_o));
  Multiplexer #(.enable("false"), .width(16)) multiplexer_4 (
    .in0(demultiplexer_9_out0), .in1(multiplexer_6_out), .out(multiplexer_4_out), .sel(conv_13_o));
  Register #(.trigger("falling"), .width(16)) AX (.D(demultiplexer_8_out0), .clk(conv_3_o), .Q(AX_q));  // open: en, clr
  conv conv_3 (.o(conv_3_o), .Input_bus_1(demultiplexer_8_out0));
  Register #(.width(16)) bx (.D(demultiplexer_8_out1), .clk(conv_5_o), .Q(bx_q));  // open: en, clr
  Multiplexer #(.enable("false"), .width(3)) multiplexer_5 (
    .in0(bit_extender_9_out), .in1(3'b000), .out(multiplexer_5_out), .sel(conv_2_o));
  Bit_Extender #(.in_width(16), .out_width(3)) bit_extender_12 (.in(demultiplexer_2_out6), .out(bit_extender_12_out));
  assign bit_extender_9_out = not_2_out ? or_4_out : 3'bz;  // Controlled_Buffer controlled_buffer_6
  not not_2 (not_2_out, conv_7_o);
  assign or_4_out = bit_extender_10_out | bit_extender_14_out | bit_extender_16_out | bit_extender_12_out | bit_extender_13_out;  // OR_Gate or_4, 3 bits wide
  Bit_Extender #(.in_width(16), .out_width(3)) bit_extender_13 (.in(demultiplexer_9_out1), .out(bit_extender_13_out));
  Bit_Extender #(.in_width(16), .out_width(3)) bit_extender_14 (.in(demultiplexer_1_out7), .out(bit_extender_14_out));
  Bit_Extender #(.in_width(16), .out_width(3)) bit_extender_15 (.in(demultiplexer_7_out1), .out(bit_extender_15_out));
  Register #(.width(16)) cx (.D(demultiplexer_8_out2), .clk(conv_4_o), .Q(cx_q));  // open: en, clr
  conv conv_4 (.o(conv_4_o), .Input_bus_1(demultiplexer_8_out2));
  Register #(.width(16)) dx (.D(demultiplexer_8_out3), .clk(conv_6_o), .Q(dx_q));  // open: en, clr
  conv conv_6 (.o(conv_6_o), .Input_bus_1(demultiplexer_8_out3));
  assign demultiplexer_5_out0 = comparator_2_eq ? multiplexer_6_out : 16'bz;  // Controlled_Buffer controlled_buffer_7
  assign data_bus = conv_7_o ? multiplexer_6_out : 16'bz;  // Controlled_Buffer controlled_buffer_8
  not not_3 (not_3_out, conv_7_o);
  assign controlled_buffer_9_out = not_3_out ? data_in : 16'bz;  // Controlled_Buffer controlled_buffer_9
  conv conv_11 (.o(conv_11_o), .Input_bus_1(multiplexer_4_out));
  assign or_5_out = demultiplexer_2_out5 | multiplexer_4_out;  // OR_Gate or_5, 16 bits wide
  conv conv_12 (.o(conv_12_o), .Input_bus_1(or_5_out));
  Counter #(.max('hffff), .ongoal("stay"), .trigger("falling"), .width(16)) SC (
    .up(conv_14_o), .clk(conv_15_o), .Q(SC_q));  // open: clr, load, count, D, carry
  conv conv_14 (.o(conv_14_o), .Input_bus_1(multiplexer_4_out));
  assign or_6_out = multiplexer_4_out | demultiplexer_2_out5;  // OR_Gate or_6, 16 bits wide
  conv conv_15 (.o(conv_15_o), .Input_bus_1(or_6_out));
  Bit_Extender #(.in_width(16), .out_width(3)) bit_extender_16 (.in(demultiplexer_2_out8), .out(bit_extender_16_out));
  and and_1 (and_1_out, demultiplexer_3_out1[7], conv_2_o_2);
  Multiplexer #(.enable("false"), .select(3), .width(16)) multiplexer_6 (
    .in0(AX_q), .in1(bx_q), .in2(cx_q), .in3(dx_q), .in4(DS_q), .in5(sflags_q), .out(multiplexer_6_out),
    .sel(multiplexer_5_out));  // open: in6, in7
  Register #(.width(16)) DS (.D(demultiplexer_8_out4), .clk(conv_8_o), .Q(DS_q));  // open: en, clr
  conv conv_8 (.o(conv_8_o), .Input_bus_1(demultiplexer_8_out4));
  Comparator #(.width(16)) comparator_4 (
    .a(multiplexer_6_out), .b(demultiplexer_2_out7), .gt(comparator_4_gt), .lt(comparator_4_lt));  // open: eq
  conv conv_10 (.o(conv_10_o), .Input_bus_1(demultiplexer_2_out5));
  assign buffer_2_out = demultiplexer_8_out5;  // Buffer buffer_2, 16 bits wide
  or or_7 (or_7_out, comparator_4_gt, comparator_4_lt);
  buf buffer_3 (buffer_3_out, conv_12_o);
  conv conv_1_dup2 (.o(conv_1_o_2), .Input_bus_1(buffer_2_out));
  conv conv_2_dup2 (.o(conv_2_o_2), .Input_bus_1(sflags_q));
  Multiplexer #(.enable("false"), .width(16)) multiplexer_7 (
    .in0({16{1'b0}}), .in1(stack_dout), .out(multiplexer_7_out), .sel(conv_10_o));
  conv conv_3_dup2 (.o(conv_3_o_2), .Input_bus_1(demultiplexer_2_out5));
  Bit_Extender #(.in_width(1)) bit_extender_17 (.in(or_7_out));  // open: out
  Register #(.width(16)) sflags (.D(buffer_2_out), .clk(conv_1_o_2), .Q(sflags_q));  // open: en, clr
  RAM #(.addrWidth(16), .dataWidth(16), .trigger("falling")) stack (
    .addr(SC_q), .we(conv_11_o), .oe(conv_3_o_2), .clk(buffer_3_out), .din(multiplexer_4_out),
    .dout(stack_dout));

  // Notes on the sheet:
  //   Control Unit
  //   ALU
  //   Stack
  //   Registers
endmodule

module alu (
  input  [15:0] in1,
  input  [15:0] in2,
  input  [1:0] func,
  output [15:0] Output_bus_1
);

  wire [15:0] adder_1_out, demultiplexer_1_out0, demultiplexer_1_out1, demultiplexer_1_out2,
       demultiplexer_1_out3, demultiplexer_2_out0, demultiplexer_2_out1, demultiplexer_2_out2,
       demultiplexer_2_out3, divider_1_out, multiplier_1_out, subtractor_1_out;

  Demultiplexer #(.enable("false"), .select(2), .width(16)) demultiplexer_1 (
    .out0(demultiplexer_1_out0), .out1(demultiplexer_1_out1), .out2(demultiplexer_1_out2),
    .out3(demultiplexer_1_out3), .in(in1), .sel(func));
  Demultiplexer #(.enable("false"), .select(2), .width(16)) demultiplexer_2 (
    .out0(demultiplexer_2_out0), .out1(demultiplexer_2_out1), .out2(demultiplexer_2_out2),
    .out3(demultiplexer_2_out3), .in(in2), .sel(func));
  Adder #(.width(16)) adder_1 (
    .a(demultiplexer_1_out0), .b(demultiplexer_2_out0), .out(adder_1_out));  // open: cin, cout
  Subtractor #(.width(16)) subtractor_1 (
    .a(demultiplexer_1_out1), .b(demultiplexer_2_out1), .out(subtractor_1_out));  // open: bin, bout
  Multiplier #(.width(16)) multiplier_1 (
    .a(demultiplexer_1_out2), .b(demultiplexer_2_out2), .out(multiplier_1_out));  // open: cin, cout
  Divider #(.width(16)) divider_1 (
    .a(demultiplexer_1_out3), .b(demultiplexer_2_out3), .out(divider_1_out));  // open: upper, rem
  assign Output_bus_1 = adder_1_out | subtractor_1_out | multiplier_1_out | divider_1_out;  // OR_Gate or_1, 16 bits wide
endmodule

module conv (
  input  [15:0] Input_bus_1,
  output o
);

  wire buffer_1_out, buffer_2_out, buffer_3_out, buffer_4_out, buffer_5_out, buffer_6_out, buffer_7_out,
       buffer_8_out, buffer_9_out, buffer_10_out, buffer_11_out, buffer_12_out, buffer_13_out, buffer_14_out,
       buffer_15_out, buffer_16_out;

  buf buffer_1 (buffer_1_out, Input_bus_1[7]);
  buf buffer_2 (buffer_2_out, Input_bus_1[0]);
  buf buffer_3 (buffer_3_out, Input_bus_1[1]);
  buf buffer_4 (buffer_4_out, Input_bus_1[2]);
  buf buffer_5 (buffer_5_out, Input_bus_1[3]);
  buf buffer_6 (buffer_6_out, Input_bus_1[4]);
  buf buffer_7 (buffer_7_out, Input_bus_1[5]);
  buf buffer_8 (buffer_8_out, Input_bus_1[6]);
  or or_1 (o, buffer_1_out, buffer_2_out, buffer_3_out, buffer_4_out, buffer_5_out, buffer_6_out, buffer_7_out, buffer_8_out, buffer_9_out, buffer_10_out, buffer_11_out, buffer_12_out, buffer_13_out, buffer_14_out, buffer_15_out, buffer_16_out);
  buf buffer_9 (buffer_9_out, Input_bus_1[8]);
  buf buffer_10 (buffer_10_out, Input_bus_1[9]);
  buf buffer_11 (buffer_11_out, Input_bus_1[10]);
  buf buffer_12 (buffer_12_out, Input_bus_1[11]);
  buf buffer_13 (buffer_13_out, Input_bus_1[12]);
  buf buffer_14 (buffer_14_out, Input_bus_1[13]);
  buf buffer_15 (buffer_15_out, Input_bus_1[14]);
  buf buffer_16 (buffer_16_out, Input_bus_1[15]);
endmodule

module lu (
  input  [15:0] in1,
  input  [15:0] in2,
  input  [7:0] f,
  output [15:0] Output_bus_1
);

  wire [2:0] bit_extender_1_out;
  wire [15:0] and_1_out, demultiplexer_1_out1, demultiplexer_1_out2, demultiplexer_1_out3,
       demultiplexer_1_out4, demultiplexer_1_out5, demultiplexer_1_out6, demultiplexer_2_out0,
       demultiplexer_2_out1, demultiplexer_2_out2, demultiplexer_2_out3, demultiplexer_2_out4,
       demultiplexer_2_out5, demultiplexer_2_out6, nand_1_out, nor_1_out, not_1_out, or_1_out, xnor_1_out,
       xor_1_out;

  Demultiplexer #(.enable("false"), .select(3), .width(16)) demultiplexer_1 (
    .out1(demultiplexer_1_out1), .out2(demultiplexer_1_out2), .out3(demultiplexer_1_out3),
    .out4(demultiplexer_1_out4), .out5(demultiplexer_1_out5), .out6(demultiplexer_1_out6), .in(in1),
    .sel(bit_extender_1_out));  // open: out0, out7
  Demultiplexer #(.enable("false"), .select(3), .width(16)) demultiplexer_2 (
    .out0(demultiplexer_2_out0), .out1(demultiplexer_2_out1), .out2(demultiplexer_2_out2),
    .out3(demultiplexer_2_out3), .out4(demultiplexer_2_out4), .out5(demultiplexer_2_out5),
    .out6(demultiplexer_2_out6), .in(in2), .sel(bit_extender_1_out));  // open: out7
  Bit_Extender #(.out_width(3)) bit_extender_1 (.in(f), .out(bit_extender_1_out));
  assign not_1_out = ~demultiplexer_2_out0;  // NOT_Gate not_1, 16 bits wide
  assign or_1_out = demultiplexer_1_out2 | demultiplexer_2_out2;  // OR_Gate or_1, 16 bits wide
  assign and_1_out = demultiplexer_1_out1 & demultiplexer_2_out1;  // AND_Gate and_1, 16 bits wide
  assign nand_1_out = ~(demultiplexer_1_out3 & demultiplexer_2_out3);  // NAND_Gate nand_1, 16 bits wide
  assign nor_1_out = ~(demultiplexer_1_out4 | demultiplexer_2_out4);  // NOR_Gate nor_1, 16 bits wide
  assign xor_1_out = demultiplexer_1_out5 ^ demultiplexer_2_out5;  // XOR_Gate xor_1, 16 bits wide
  assign xnor_1_out = ~(demultiplexer_1_out6 ^ demultiplexer_2_out6);  // XNOR_Gate xnor_1, 16 bits wide
  Multiplexer #(.enable("false"), .select(3), .width(16)) multiplexer_1 (
    .in0(not_1_out), .in1(and_1_out), .in2(or_1_out), .in3(nand_1_out), .in4(nor_1_out), .in5(xor_1_out),
    .in6(xnor_1_out), .out(Output_bus_1), .sel(bit_extender_1_out));  // open: in7
endmodule

module motherboard (
);

  wire clock_1_out, clock_2_out, clock_3_out, conv_1_o, conv_2_o, conv_3_o, conv_4_o, conv_5_o,
       counter_3_carry, main_1_ram_enable, not_1_out, or_1_out, por_1_out, rgb_video_1_p1, rgb_video_1_p7;
  wire [5:0] rgb_video_1_p4;
  wire [6:0] bit_extender_1_out, counter_3_q;
  wire [15:0] controlled_buffer_1_out, counter_1_q, main_1_adrbus, main_1_data_addrbus, main_1_data_bus,
       main_1_out_69, main_1_out_70, main_1_out_71, undriven, undriven_2;
  wire [44:0] rom_1_data;

  ROM #(.addrWidth(16), .dataWidth(45)) rom_1 (.addr(main_1_adrbus), .data(rom_1_data));
  Clock clock_1 (.out(clock_1_out));
  main main_1 (
    .data_addrbus(main_1_data_addrbus), .adrbus(main_1_adrbus), .data_bus(main_1_data_bus),
    .ram_enable(main_1_ram_enable), .out_69(main_1_out_69), .out_70(main_1_out_70), .out_71(main_1_out_71),
    .ramcode_in(rom_1_data), .data_in(undriven_2), .in_25(undriven), .CLK(clock_1_out));  // open: out_40, out_41, out_42, out_43, out_44, out_45, out_46, out_47, out_48, out_49, out_50, out_51, out_52, out_53, out_54, out_55, out_56, out_57, out_58, out_59, out_60, out_61, out_62, out_63, out_64, out_65, out_66, out_67, out_68, in_4, in_5, in_6, in_7, in_8, in_9, in_10, in_11, in_12, in_13, in_14, in_15, in_16, in_17, in_18, in_19, in_20, in_21, in_22, in_23, in_24, in_26, in_27, in_28, in_29, in_30, in_31, in_32, in_33, in_34, in_35
  conv conv_1 (.o(conv_1_o), .Input_bus_1(main_1_data_bus));
  conv conv_2 (.o(conv_2_o), .Input_bus_1(main_1_data_addrbus));
  or or_1 (or_1_out, conv_2_o, por_1_out);
  POR #(.PorHighDuration(1)) por_1 (.out(por_1_out));
  Clock clock_2 (.out(clock_2_out));
  RAM #(.addrWidth(16), .dataWidth(16)) system_ram (
    .addr(main_1_data_addrbus), .we(conv_1_o), .oe(main_1_ram_enable), .clk(or_1_out), .din(main_1_data_bus));  // open: dout
  conv conv_3 (.o(conv_3_o), .Input_bus_1(main_1_out_69));
  assign controlled_buffer_1_out = conv_3_o ? main_1_out_69 : 16'bz;  // Controlled_Buffer controlled_buffer_1
  assign controlled_buffer_1_out = not_1_out ? counter_1_q : 16'bz;  // Controlled_Buffer controlled_buffer_2
  not not_1 (not_1_out, conv_3_o);
  Counter #(.max('h1000), .width(16)) counter_1 (
    .Q(counter_1_q), .clk(clock_2_out));  // open: load, D, count, carry, up, clr
  conv conv_4 (.o(conv_4_o), .Input_bus_1(main_1_out_70));
  Clock clock_3 (.out(clock_3_out));
  conv conv_5 (.o(conv_5_o), .Input_bus_1(main_1_out_71));
  Bit_Extender #(.in_width(16), .out_width(7)) bit_extender_1 (.in(main_1_out_71), .out(bit_extender_1_out));
  TTY #(.trigger("falling")) tty_1 (.data(bit_extender_1_out), .clk(clock_3_out), .we(conv_5_o));  // open: clr
  Counter #(.max('h40), .width(16)) counter_2 (.clk(clock_2_out));  // open: load, D, count, Q, carry, up, clr
  Counter #(.max('h7f), .trigger("falling"), .width(7)) counter_3 (
    .clk(rgb_video_1_p1), .carry(counter_3_carry), .Q(counter_3_q));  // open: clr, load, up, count, D
  // RGB_Video #(.height(64)) rgb_video_1: pin names not known; wires that end beside it: rgb_video_1_p1, rgb_video_1_p1, counter_3_q, rgb_video_1_p4, 8'h7, counter_3_carry, rgb_video_1_p7
  Clock pixel_clock (.out(rgb_video_1_p1));
  Counter #(.max('h3f), .trigger("falling"), .width(6)) counter_4 (
    .Q(rgb_video_1_p4), .carry(rgb_video_1_p7), .clk(counter_3_carry));  // open: load, D, count, up, clr

  // Notes on the sheet:
  //   contents of rom_1 (hex, n*v repeats v):
  //   30064000000 80000000000
endmodule
